// Logisim project ALUandShifter.circ as structural Verilog: 11 circuits, main circuit main
module main (
  input  [5:0] in_1,
  input  [31:0] A,
  input  [31:0] B,
  input  [1:0] Shifter,
  output Z,
  output N,
  output [31:0] C_Bus
);

  wire [31:0] n32_bit_alu_1_output;

  _32_Bit_ALU u_32_bit_alu_1 (
    .Output(n32_bit_alu_1_output), .Z(Z), .N(N), .A(A), .B(B), .Carry_in(in_1[0]), .ENB(in_1[2]),
    .ENA(in_1[3]), .INVA(in_1[1]), .F1(in_1[4]), .F0(in_1[5]));
  Shifter shifter_1 (.SLL8(Shifter[1]), .SRA1(Shifter[0]), .C_Bus(n32_bit_alu_1_output), .Output(C_Bus));

  // Notes on the sheet:
  //   Matthew Matze
endmodule

module _1_Bit_ALU (
  input  INVA,
  input  A,
  input  ENA,
  input  B,
  input  Carry_In,
  input  ENB,
  input  F0,
  input  F1,
  output Output,
  output Carry_Out
);

  wire and_1_out, and_2_out, decoder_1_enable_0, decoder_1_enable_1, decoder_1_enable_2, decoder_1_enable_3,
       full_adder_1_sum, logic_unit_1_output_0, logic_unit_1_output_1, logic_unit_1_output_2, xor_1_out;

  and and_1 (and_1_out, A, ENA);
  and and_2 (and_2_out, B, ENB);
  xor xor_1 (xor_1_out, INVA, and_1_out);
  Decoder decoder_1 (
    .F0(F0), .F1(F1), .Enable_0(decoder_1_enable_0), .Enable_1(decoder_1_enable_1),
    .Enable_2(decoder_1_enable_2), .Enable_3(decoder_1_enable_3));
  Logic_Unit logic_unit_1 (
    .A(xor_1_out), .B(and_2_out), .Output_0(logic_unit_1_output_0), .Output_1(logic_unit_1_output_1),
    .Output_2(logic_unit_1_output_2), .Enable_0(decoder_1_enable_0), .Enable_1(decoder_1_enable_1),
    .Enable_2(decoder_1_enable_2));
  Full_Adder full_adder_1 (
    .A(xor_1_out), .B(and_2_out), .Enable(decoder_1_enable_3), .Sum(full_adder_1_sum), .Carry_In(Carry_In),
    .Carry_Out(Carry_Out));
  or or_1 (Output, logic_unit_1_output_0, logic_unit_1_output_1, logic_unit_1_output_2, full_adder_1_sum);
endmodule

module Decoder (
  input  F0,
  input  F1,
  output Enable_0,
  output Enable_1,
  output Enable_2,
  output Enable_3
);

  wire not_1_out, not_2_out, not_3_out, not_4_out;

  not not_1 (not_1_out, F0);
  not not_2 (not_2_out, F1);
  not not_3 (not_3_out, F0);
  not not_4 (not_4_out, F1);
  and and_1 (Enable_0, not_1_out, not_2_out);
  and and_2 (Enable_1, F1, not_3_out);
  and and_3 (Enable_2, F0, not_4_out);
  and and_4 (Enable_3, F1, F0);
endmodule

module Full_Adder (
  input  Carry_In,
  input  A,
  input  B,
  input  Enable,
  output Sum,
  output Carry_Out
);

  wire and_1_out, and_2_out, xor_1_out, xor_2_out;

  and and_1 (and_1_out, A, B, Enable);
  or or_1 (Carry_Out, and_1_out, and_2_out);
  xor xor_1 (xor_1_out, A, B);
  and and_2 (and_2_out, Enable, xor_1_out, Carry_In);
  xor xor_2 (xor_2_out, Carry_In, xor_1_out);
  and and_3 (Sum, xor_2_out, Enable);
endmodule

module Logic_Unit (
  input  A,
  input  B,
  input  Enable_0,
  input  Enable_1,
  input  Enable_2,
  output Output_0,
  output Output_1,
  output Output_2
);

  wire and_1_out, not_1_out, or_1_out;

  and and_1 (and_1_out, A, B);
  or or_1 (or_1_out, A, B);
  not not_1 (not_1_out, B);
  and and_2 (Output_0, Enable_0, and_1_out);
  and and_3 (Output_1, Enable_1, or_1_out);
  and and_4 (Output_2, Enable_2, not_1_out);
endmodule

module _8_Bit_ALU (
  input  [7:0] B,
  input  [7:0] A,
  input  ENB,
  input  ENA,
  input  INVA,
  input  F1,
  input  F0,
  input  Carry_In,
  output [7:0] out_9,
  output Z,
  output N,
  output Carry_Out
);

  wire n1_bit_alu_1_carry_out, n1_bit_alu_2_carry_out, n1_bit_alu_3_carry_out, n1_bit_alu_4_carry_out,
       n1_bit_alu_5_carry_out, n1_bit_alu_6_carry_out, n1_bit_alu_7_carry_out;

  _1_Bit_ALU u_1_bit_alu_1 (
    .A(A[0]), .B(B[0]), .F0(F0), .F1(F1), .Output(out_9[0]), .Carry_Out(n1_bit_alu_1_carry_out),
    .Carry_In(Carry_In), .INVA(INVA), .ENA(ENA), .ENB(ENB));
  _1_Bit_ALU u_1_bit_alu_2 (
    .A(A[1]), .B(B[1]), .F0(F0), .F1(F1), .Output(out_9[1]), .Carry_Out(n1_bit_alu_2_carry_out),
    .Carry_In(n1_bit_alu_1_carry_out), .INVA(INVA), .ENA(ENA), .ENB(ENB));
  _1_Bit_ALU u_1_bit_alu_3 (
    .A(A[2]), .B(B[2]), .F0(F0), .F1(F1), .Output(out_9[2]), .Carry_Out(n1_bit_alu_3_carry_out),
    .Carry_In(n1_bit_alu_2_carry_out), .INVA(INVA), .ENA(ENA), .ENB(ENB));
  _1_Bit_ALU u_1_bit_alu_4 (
    .A(A[3]), .B(B[3]), .F0(F0), .F1(F1), .Output(out_9[3]), .Carry_Out(n1_bit_alu_4_carry_out),
    .Carry_In(n1_bit_alu_3_carry_out), .INVA(INVA), .ENA(ENA), .ENB(ENB));
  _1_Bit_ALU u_1_bit_alu_5 (
    .A(A[4]), .B(B[4]), .F0(F0), .F1(F1), .Output(out_9[4]), .Carry_Out(n1_bit_alu_5_carry_out),
    .Carry_In(n1_bit_alu_4_carry_out), .INVA(INVA), .ENA(ENA), .ENB(ENB));
  _1_Bit_ALU u_1_bit_alu_6 (
    .A(A[5]), .B(B[5]), .F0(F0), .F1(F1), .Output(out_9[5]), .Carry_Out(n1_bit_alu_6_carry_out),
    .Carry_In(n1_bit_alu_5_carry_out), .INVA(INVA), .ENA(ENA), .ENB(ENB));
  _1_Bit_ALU u_1_bit_alu_7 (
    .A(A[6]), .B(B[6]), .F0(F0), .F1(F1), .Output(out_9[6]), .Carry_Out(n1_bit_alu_7_carry_out),
    .Carry_In(n1_bit_alu_6_carry_out), .INVA(INVA), .ENA(ENA), .ENB(ENB));
  _1_Bit_ALU u_1_bit_alu_8 (
    .A(A[7]), .B(B[7]), .F0(F0), .F1(F1), .Output(N), .Carry_Out(Carry_Out),
    .Carry_In(n1_bit_alu_7_carry_out), .INVA(INVA), .ENA(ENA), .ENB(ENB));
  nor nor_1 (Z, out_9[0], out_9[1], out_9[2], out_9[3], out_9[4], out_9[5], out_9[6], N);

  assign out_9[7] = N;

  // Notes on the sheet:
  //   Output
endmodule

module _1_Bit_Tester (
  input  in_1,
  input  in_2,
  input  in_3,
  input  in_4,
  input  in_5,
  input  in_6,
  input  in_7,
  input  in_8,
  input  in_9,
  input  in_10,
  input  in_11,
  input  in_12,
  input  in_13,
  input  in_14,
  input  in_15,
  output out_16,
  output out_17,
  output out_18,
  output out_19
);

  _1_Bit_ALU u_1_bit_alu_1 (
    .A(in_3), .B(in_5), .F0(in_7), .F1(in_8), .Output(out_16), .Carry_Out(out_17), .Carry_In(in_1),
    .INVA(in_2), .ENA(in_4), .ENB(in_6));
  _1_Bit_ALU u_1_bit_alu_2 (
    .A(in_10), .B(in_12), .F0(in_14), .F1(in_15), .Output(out_18), .Carry_Out(out_19), .Carry_In(out_17),
    .INVA(in_9), .ENA(in_11), .ENB(in_13));
endmodule

module _32_Bit_ALU (
  input  Carry_in,
  input  ENB,
  input  ENA,
  input  INVA,
  input  F1,
  input  F0,
  input  [31:0] A,
  input  [31:0] B,
  output [31:0] Output,
  output Z,
  output N
);

  wire n8_bit_alu_1_carry_out, n8_bit_alu_1_z, n8_bit_alu_2_carry_out, n8_bit_alu_2_z,
       n8_bit_alu_3_carry_out, n8_bit_alu_3_z, n8_bit_alu_4_z;

  _8_Bit_ALU u_8_bit_alu_1 (
    .B(B[7:0]), .A(A[7:0]), .out_9(Output[7:0]), .ENB(ENB), .ENA(ENA), .INVA(INVA), .F1(F1), .F0(F0),
    .Carry_In(Carry_in), .Carry_Out(n8_bit_alu_1_carry_out), .Z(n8_bit_alu_1_z));  // open: N
  _8_Bit_ALU u_8_bit_alu_2 (
    .B(B[15:8]), .A(A[15:8]), .out_9(Output[15:8]), .ENB(ENB), .ENA(ENA), .INVA(INVA), .F1(F1), .F0(F0),
    .Carry_In(n8_bit_alu_1_carry_out), .Carry_Out(n8_bit_alu_2_carry_out), .Z(n8_bit_alu_2_z));  // open: N
  _8_Bit_ALU u_8_bit_alu_3 (
    .B(B[23:16]), .A(A[23:16]), .out_9(Output[23:16]), .ENB(ENB), .ENA(ENA), .INVA(INVA), .F1(F1), .F0(F0),
    .Carry_In(n8_bit_alu_2_carry_out), .Carry_Out(n8_bit_alu_3_carry_out), .Z(n8_bit_alu_3_z));  // open: N
  _8_Bit_ALU u_8_bit_alu_4 (
    .B(B[31:24]), .A(A[31:24]), .out_9(Output[31:24]), .ENB(ENB), .ENA(ENA), .INVA(INVA), .F1(F1), .F0(F0),
    .Carry_In(n8_bit_alu_3_carry_out), .Z(n8_bit_alu_4_z), .N(N));  // open: Carry_Out
  and and_1 (Z, n8_bit_alu_1_z, n8_bit_alu_2_z, n8_bit_alu_3_z, n8_bit_alu_4_z);
endmodule

module Shifter (
  input  [31:0] C_Bus,
  input  SLL8,
  input  SRA1,
  output [31:0] Output
);

  wire [31:0] sll8_1_output;

  SLL8 sll8_1 (.in_2(1'b0), .in_3(1'b0), .in_4(1'b0), .SLL8(SLL8), .in_6(1'b0), .Output(sll8_1_output), .C_Bus(C_Bus));
  SRA1 sra1_1 (.SRA1(SRA1), .in_3(1'b0), .in_4(1'b0), .in_5(1'b0), .in_6(1'b0), .Output(Output), .C_Bus(sll8_1_output));
endmodule

module SRA1 (
  input  [31:0] C_Bus,
  input  SRA1,
  input  in_3,
  input  in_4,
  input  in_5,
  input  in_6,
  output [31:0] Output
);

  Shifter_part #(.width(32), .shift("ar")) shifter_1 (
    .in(C_Bus), .\dist ({in_6, in_5, in_4, in_3, SRA1}), .out(Output));
endmodule

module SLL8 (
  input  [31:0] C_Bus,
  input  in_2,
  input  in_3,
  input  in_4,
  input  SLL8,
  input  in_6,
  output [31:0] Output
);

  Shifter_part #(.width(32)) shifter_1 (.in(C_Bus), .\dist ({in_6, SLL8, in_4, in_3, in_2}), .out(Output));
endmodule
