// Logisim project Machine.circ as structural Verilog: 19 circuits, main circuit main
module main (
);

  wire clock_1_out, decoder_1_out0, decoder_1_out1, decoder_1_out2, decoder_1_out3, decoder_1_out4,
       decoder_1_out5, decoder_1_out6, decoder_1_out7, decoder_1_out8, high_bit_1_high_bit,
       junction_box_1_out_4, mir_1_jmpc;
  wire [1:0] main_1_n, mir_1_n_z, mir_1_out_5;
  wire [2:0] mir_1_out_8;
  wire [3:0] mir_1_out_9;
  wire [5:0] mir_1_out_6;
  wire [7:0] junction_box_1_out_5, mbr_1_junction_box, ram_1_mbr;
  wire [8:0] mir_1_out_4, mir_1_out_7, mpc_1_out_4;
  wire [15:0] control_store_1_out_3;
  wire [19:0] control_store_1_out_2;
  wire [31:0] b_bus_1_out_19, c_bus_1_out_2, c_bus_1_out_3, c_bus_1_out_4, c_bus_1_out_5, c_bus_1_out_6,
       c_bus_1_out_7, c_bus_1_out_8, c_bus_1_out_9, c_bus_1_out_10, cpp_1_b_bus_2, h_1_a_bus, lv_1_b_bus_2,
       main_1_c_bus, mar_1_ram, mbr_1_b_bus_3, mbr_1_b_bus_4, mdr_1_b_bus_2, opc_1_b_bus_2, pc_1_b_bus_2,
       pc_1_ram, ram_1_mdrout, sp_1_b_bus_2, tos_1_b_bus_2;

  RAM ram_1 (
    .\type (1'b0), .Read(mir_1_out_8[1]), .Fetch(mir_1_out_8[0]), .MBR(ram_1_mbr), .clear(1'b0),
    .MDROUT(ram_1_mdrout), .MAR(mar_1_ram), .PC(pc_1_ram), .Write(mir_1_out_8[2]), .MDRIN(ram_1_mdrout),
    .clear_2(1'b0));
  C_Bus c_bus_1 (
    .in_1(main_1_c_bus), .out_2(c_bus_1_out_2), .out_3(c_bus_1_out_3), .out_4(c_bus_1_out_4),
    .out_5(c_bus_1_out_5), .out_6(c_bus_1_out_6), .out_7(c_bus_1_out_7), .out_8(c_bus_1_out_8),
    .out_9(c_bus_1_out_9), .out_10(c_bus_1_out_10));
  MAR mar_1 (.C_Bus(c_bus_1_out_2), .RAM(mar_1_ram), .Clock(clock_1_out), .Enable_C_Bus(mir_1_out_7[0]));
  MDR mdr_1 (
    .C_Bus(c_bus_1_out_3), .B_Bus_2(mdr_1_b_bus_2), .Clock(clock_1_out), .B_Bus(decoder_1_out0),
    .C_Bus_2(mir_1_out_7[1]), .RAM_2(ram_1_mdrout), .RAM(ram_1_mdrout));
  PC pc_1 (
    .C_Bus(c_bus_1_out_4), .B_Bus_2(pc_1_b_bus_2), .C_Bus_2(mir_1_out_7[2]), .Clock(clock_1_out),
    .B_Bus(decoder_1_out1), .RAM(pc_1_ram));
  MBR mbr_1 (
    .RAM(ram_1_mbr), .B_Bus_3(mbr_1_b_bus_3), .B_Bus(decoder_1_out2), .B_Bus_4(mbr_1_b_bus_4),
    .Clock(clock_1_out), .B_Bus_2(decoder_1_out3), .Junction_Box(mbr_1_junction_box));
  SP sp_1 (
    .C_Bus(c_bus_1_out_5), .B_Bus_2(sp_1_b_bus_2), .C_Bus_2(mir_1_out_7[3]), .Clock(clock_1_out),
    .B_Bus(decoder_1_out4));
  LV lv_1 (
    .C_Bus(c_bus_1_out_6), .B_Bus_2(lv_1_b_bus_2), .C_Bus_2(mir_1_out_7[4]), .Clock(clock_1_out),
    .B_Bus(decoder_1_out5));
  CPP cpp_1 (
    .C_Bus(c_bus_1_out_7), .B_Bus_2(cpp_1_b_bus_2), .C_Bus_2(mir_1_out_7[5]), .Clock(clock_1_out),
    .B_Bus(decoder_1_out6));
  TOS tos_1 (
    .C_Bus(c_bus_1_out_8), .B_Bus_2(tos_1_b_bus_2), .C_Bus_2(mir_1_out_7[6]), .Clock(clock_1_out),
    .B_Bus(decoder_1_out7));
  OPC opc_1 (
    .C_Bus(c_bus_1_out_9), .B_Bus_2(opc_1_b_bus_2), .C_Bus_2(mir_1_out_7[7]), .Clock(clock_1_out),
    .B_Bus(decoder_1_out8));
  H h_1 (.C_Bus(c_bus_1_out_10), .C_Bus_2(mir_1_out_7[8]), .Clock(clock_1_out), .A_Bus(h_1_a_bus));
  Clock clock_1 (.out(clock_1_out));
  ALUandShifter_main main_1 (
    .Z(main_1_n[1]), .N(main_1_n[0]), .A(h_1_a_bus), .B(b_bus_1_out_19), .Shifter(mir_1_out_5),
    .in_1(mir_1_out_6), .C_Bus(main_1_c_bus));
  Decoder #(.select(4)) decoder_1 (
    .out0(decoder_1_out0), .out1(decoder_1_out1), .out2(decoder_1_out2), .out3(decoder_1_out3),
    .out4(decoder_1_out4), .out5(decoder_1_out5), .out6(decoder_1_out6), .out7(decoder_1_out7),
    .out8(decoder_1_out8), .sel(mir_1_out_9));  // open: out9, out10, out11, out12, out13, out14, out15, en
  B_Bus b_bus_1 (
    .in_3(pc_1_b_bus_2), .in_5(mbr_1_b_bus_3), .in_7(mbr_1_b_bus_4), .in_9(sp_1_b_bus_2),
    .in_11(lv_1_b_bus_2), .in_13(cpp_1_b_bus_2), .in_15(tos_1_b_bus_2), .in_17(opc_1_b_bus_2),
    .in_1(mdr_1_b_bus_2), .in_2(decoder_1_out0), .in_4(decoder_1_out1), .in_6(decoder_1_out2),
    .in_8(decoder_1_out3), .in_10(decoder_1_out4), .in_12(decoder_1_out5), .in_14(decoder_1_out6),
    .in_16(decoder_1_out7), .in_18(decoder_1_out8), .out_19(b_bus_1_out_19));
  MPC mpc_1 (.out_4(mpc_1_out_4), .in_2(high_bit_1_high_bit), .in_3(junction_box_1_out_4), .in_1(junction_box_1_out_5));
  High_Bit high_bit_1 (.High_Bit(high_bit_1_high_bit), .ALU(main_1_n), .MIR(mir_1_n_z), .Clock(clock_1_out));
  Junction_Box junction_box_1 (
    .MBR(mbr_1_junction_box), .JMPC(mir_1_jmpc), .out_4(junction_box_1_out_4), .out_5(junction_box_1_out_5),
    .Addr(mir_1_out_4));
  Control_Store control_store_1 (.in_1(mpc_1_out_4), .out_2(control_store_1_out_2), .out_3(control_store_1_out_3));
  MIR mir_1 (
    .in_1(control_store_1_out_2), .in_2(control_store_1_out_3), .out_4(mir_1_out_4), .N_Z(mir_1_n_z),
    .out_5(mir_1_out_5), .out_6(mir_1_out_6), .in_3(clock_1_out), .out_7(mir_1_out_7), .out_8(mir_1_out_8),
    .out_9(mir_1_out_9), .JMPC(mir_1_jmpc));
endmodule

module MAR (
  input  [31:0] C_Bus,
  input  Enable_C_Bus,
  input  Clock,
  output [31:0] RAM
);

  Register #(.width(32), .trigger("falling")) MAR (.D(C_Bus), .en(Enable_C_Bus), .Q(RAM), .clk(Clock));  // open: clr
endmodule

module MDR (
  input  [31:0] C_Bus,
  input  Clock,
  input  B_Bus,
  input  C_Bus_2,
  input  [31:0] RAM,
  output [31:0] B_Bus_2,
  output [31:0] RAM_2
);

  wire not_1_out;
  wire [31:0] controlled_buffer_1_out;

  assign controlled_buffer_1_out = C_Bus_2 ? C_Bus : 32'bz;  // Controlled_Buffer controlled_buffer_1
  Register #(.width(32), .trigger("falling")) MDR (
    .D(controlled_buffer_1_out), .en(C_Bus_2), .Q(RAM_2), .clk(Clock));  // open: clr
  assign controlled_buffer_1_out = not_1_out ? RAM : 32'bz;  // Controlled_Buffer controlled_buffer_2
  not not_1 (not_1_out, C_Bus_2);
  assign B_Bus_2 = B_Bus ? RAM_2 : 32'bz;  // Controlled_Buffer controlled_buffer_3
endmodule

module PC (
  input  [31:0] C_Bus,
  input  C_Bus_2,
  input  Clock,
  input  B_Bus,
  output [31:0] B_Bus_2,
  output [31:0] RAM
);

  Register #(.width(32), .trigger("falling")) PC (.D(C_Bus), .en(C_Bus_2), .Q(RAM), .clk(Clock));  // open: clr
  assign B_Bus_2 = B_Bus ? RAM : 32'bz;  // Controlled_Buffer controlled_buffer_1
endmodule

module MBR (
  input  [7:0] RAM,
  input  B_Bus,
  input  B_Bus_2,
  input  Clock,
  output [7:0] Junction_Box,
  output [31:0] B_Bus_3,
  output [31:0] B_Bus_4
);

  wire [31:0] bit_extender_1_out, bit_extender_2_out, MBR_q, MBRU_q;

  assign bit_extender_1_out = {{24{RAM[7]}}, RAM};  // Bit_Extender bit_extender_1
  assign bit_extender_2_out = {{24{1'b0}}, RAM};  // Bit_Extender bit_extender_2
  Register #(.width(32), .trigger("falling")) MBR (
    .D(bit_extender_1_out), .en(1'b1), .Q(MBR_q), .clk(Clock));  // open: clr
  Register #(.width(32), .trigger("falling")) MBRU (
    .D(bit_extender_2_out), .en(1'b1), .Q(MBRU_q), .clk(Clock));  // open: clr
  Bit_Extender #(.in_width(32), .out_width(8), .\type ("sign")) bit_extender_3 (.in(MBR_q), .out(Junction_Box));
  assign B_Bus_3 = B_Bus ? MBR_q : 32'bz;  // Controlled_Buffer controlled_buffer_1
  assign B_Bus_4 = B_Bus_2 ? MBRU_q : 32'bz;  // Controlled_Buffer controlled_buffer_2
endmodule

module SP (
  input  [31:0] C_Bus,
  input  C_Bus_2,
  input  Clock,
  input  B_Bus,
  output [31:0] B_Bus_2
);

  wire [31:0] SP_q;

  Register #(.width(32), .trigger("falling")) SP (.D(C_Bus), .en(C_Bus_2), .Q(SP_q), .clk(Clock));  // open: clr
  assign B_Bus_2 = B_Bus ? SP_q : 32'bz;  // Controlled_Buffer controlled_buffer_1
endmodule

module LV (
  input  [31:0] C_Bus,
  input  C_Bus_2,
  input  Clock,
  input  B_Bus,
  output [31:0] B_Bus_2
);

  wire [31:0] LV_q;

  Register #(.width(32), .trigger("falling")) LV (.D(C_Bus), .en(C_Bus_2), .Q(LV_q), .clk(Clock));  // open: clr
  assign B_Bus_2 = B_Bus ? LV_q : 32'bz;  // Controlled_Buffer controlled_buffer_1
endmodule

module CPP (
  input  [31:0] C_Bus,
  input  C_Bus_2,
  input  Clock,
  input  B_Bus,
  output [31:0] B_Bus_2
);

  wire [31:0] LV_q;

  Register #(.width(32), .trigger("falling")) LV (.D(C_Bus), .en(C_Bus_2), .Q(LV_q), .clk(Clock));  // open: clr
  assign B_Bus_2 = B_Bus ? LV_q : 32'bz;  // Controlled_Buffer controlled_buffer_1
endmodule

module TOS (
  input  [31:0] C_Bus,
  input  C_Bus_2,
  input  Clock,
  input  B_Bus,
  output [31:0] B_Bus_2
);

  wire [31:0] LV_q;

  Register #(.width(32), .trigger("falling")) LV (.D(C_Bus), .en(C_Bus_2), .Q(LV_q), .clk(Clock));  // open: clr
  assign B_Bus_2 = B_Bus ? LV_q : 32'bz;  // Controlled_Buffer controlled_buffer_1
endmodule

module OPC (
  input  [31:0] C_Bus,
  input  C_Bus_2,
  input  Clock,
  input  B_Bus,
  output [31:0] B_Bus_2
);

  wire [31:0] LV_q;

  Register #(.width(32), .trigger("falling")) LV (.D(C_Bus), .en(C_Bus_2), .Q(LV_q), .clk(Clock));  // open: clr
  assign B_Bus_2 = B_Bus ? LV_q : 32'bz;  // Controlled_Buffer controlled_buffer_1
endmodule

module H (
  input  [31:0] C_Bus,
  input  C_Bus_2,
  input  Clock,
  output [31:0] A_Bus
);

  Register #(.width(32), .trigger("falling")) LV (.D(C_Bus), .en(C_Bus_2), .Q(A_Bus), .clk(Clock));  // open: clr
endmodule

module B_Bus (
  input  [31:0] in_1,
  input  in_2,
  input  [31:0] in_3,
  input  in_4,
  input  [31:0] in_5,
  input  in_6,
  input  [31:0] in_7,
  input  in_8,
  input  [31:0] in_9,
  input  in_10,
  input  [31:0] in_11,
  input  in_12,
  input  [31:0] in_13,
  input  in_14,
  input  [31:0] in_15,
  input  in_16,
  input  [31:0] in_17,
  input  in_18,
  output [31:0] out_19
);

  assign out_19 = in_2 ? in_1 : 32'bz;  // Controlled_Buffer controlled_buffer_1
  assign out_19 = in_4 ? in_3 : 32'bz;  // Controlled_Buffer controlled_buffer_2
  assign out_19 = in_6 ? in_5 : 32'bz;  // Controlled_Buffer controlled_buffer_3
  assign out_19 = in_8 ? in_7 : 32'bz;  // Controlled_Buffer controlled_buffer_4
  assign out_19 = in_10 ? in_9 : 32'bz;  // Controlled_Buffer controlled_buffer_5
  assign out_19 = in_12 ? in_11 : 32'bz;  // Controlled_Buffer controlled_buffer_6
  assign out_19 = in_14 ? in_13 : 32'bz;  // Controlled_Buffer controlled_buffer_7
  assign out_19 = in_16 ? in_15 : 32'bz;  // Controlled_Buffer controlled_buffer_8
  assign out_19 = in_18 ? in_17 : 32'bz;  // Controlled_Buffer controlled_buffer_9
endmodule

module MIR (
  input  [19:0] in_1,
  input  [15:0] in_2,
  input  in_3,
  output [8:0] out_4,
  output [1:0] out_5,
  output [5:0] out_6,
  output [8:0] out_7,
  output [2:0] out_8,
  output [3:0] out_9,
  output JMPC,
  output [1:0] N_Z
);

  Register #(.width(9)) Addr (.D(in_1[19:11]), .en(1'b1), .Q(out_4), .clk(in_3));  // open: clr
  Register #(.width(2)) Shifter (.D(in_1[7:6]), .en(1'b1), .Q(out_5), .clk(in_3));  // open: clr
  Register #(.width(3)) JAM (.D(in_1[10:8]), .en(1'b1), .Q({JMPC, N_Z}), .clk(in_3));  // open: clr
  Register #(.width(6)) ALU (.D(in_1[5:0]), .en(1'b1), .Q(out_6), .clk(in_3));  // open: clr
  Register #(.width(9)) C (.D(in_2[15:7]), .en(1'b1), .Q(out_7), .clk(in_3));  // open: clr
  Register #(.width(3)) Mem (.D(in_2[6:4]), .en(1'b1), .Q(out_8), .clk(in_3));  // open: clr
  Register #(.width(4)) B (.D(in_2[3:0]), .en(1'b1), .Q(out_9), .clk(in_3));  // open: clr
endmodule

module C_Bus (
  input  [31:0] in_1,
  output [31:0] out_2,
  output [31:0] out_3,
  output [31:0] out_4,
  output [31:0] out_5,
  output [31:0] out_6,
  output [31:0] out_7,
  output [31:0] out_8,
  output [31:0] out_9,
  output [31:0] out_10
);


  assign out_2 = in_1;
  assign out_3 = in_1;
  assign out_4 = in_1;
  assign out_5 = in_1;
  assign out_6 = in_1;
  assign out_7 = in_1;
  assign out_8 = in_1;
  assign out_9 = in_1;
  assign out_10 = in_1;
endmodule

module Control_Store (
  input  [8:0] in_1,
  output [19:0] out_2,
  output [15:0] out_3
);

  ROM #(.addrWidth(9), .dataWidth(20)) rom_1 (.addr(in_1), .data(out_2));  // open: sel
  ROM #(.addrWidth(9), .dataWidth(16)) rom_2 (.addr(in_1), .data(out_3));  // open: sel

  // Notes on the sheet:
  //   contents of rom_1 (hex, n*v repeats v):
  //   1000 20835 435 2014 103c 3014 103f 4014 100c 5014 101c 1014 6800 1014 7814 8814 b035 9014 a036 e035
  //   1018 c014 b835 1014 c83c d035 d835 1014 e83c f014 f836 10035 1014 80400 11894 1201c c83c 13094 1381c
  //   e83c 14894 1501c c83c 1603c 16835 17014 17835 103c 18835 19094 1981c 1a03c 1000 1b814 e014 1c014 a14
  //   1d014 1d814 914 1e036 1f014 1f814 20014 93f 21035 1000 22080 2281c 2303c 23835 24014 24835 25094
  //   2581c 26035 2683f 27035 27835 28080 2881c 2903d 29814 2a014 2a835 2b014 2c035 6036 1014 5835 2d800
  //   2e014 2e835 2f014 30814 7036 1835 31014 1014 32800 2836 25*32800 3836 32800 4836 32800 32800 32800
  //   15814 20*32800 1c836 32800 1a836 32800 32800 32800 1e036 7*32800 18036 4*32800 2d014 9*32800 21835
  //   13*32800 10835 58*32800 18036 19*32800 11035 32*32800 c835 9*32800
  //   contents of rom_2 (hex, n*v repeats v):
  //   0 201 211 8007 2100 8007 2140 8007 2140 8007 2140 147 0 2000 84 8040 484 107 c4 211 2000 8005 211
  //   2142 a3 484 251 2000 83 147 4a4 211 2000 0 8003 8003 a5 8003 8003 a5 8003 8003 a6 a3 211 8000 211
  //   142 211 8002 8003 218 0 4007 8005 2000 8 4007 2000 8 484 8020 4007 2000 8 211 0 8003 8003 a6 4001
  //   210 211 8003 8003 211 2004 2087 211 8003 8003 144 480 148 484 145 211 4a4 807 484 0 8a0 85 230 84 a4
  //   4a4 800 147 0 4a4 25*0 4a4 0 4a4 0 0 0 8005 20*0 4a4 0 4a4 0 0 0 4a4 7*0 4001 4*0 4a5 9*0 211 13*0
  //   211 58*0 4001 19*0 211 32*0 211
endmodule

module Junction_Box (
  input  JMPC,
  input  [7:0] MBR,
  input  [8:0] Addr,
  output out_4,
  output [7:0] out_5
);

  wire not_1_out;

  assign out_5 = JMPC ? MBR : 8'bz;  // Controlled_Buffer controlled_buffer_1
  assign out_5 = not_1_out ? Addr[7:0] : 8'bz;  // Controlled_Buffer controlled_buffer_2
  not not_1 (not_1_out, JMPC);

  assign out_4 = Addr[8];
endmodule

module MPC (
  input  [7:0] in_1,
  input  in_2,
  input  in_3,
  output [8:0] out_4
);

  and and_1 (out_4[8], in_2, in_3);

  assign out_4[7:0] = in_1;
endmodule

module High_Bit (
  input  [1:0] MIR,
  input  Clock,
  input  [1:0] ALU,
  output High_Bit
);

  wire and_1_out, and_2_out, d_ff_1_q, d_ff_2_q;

  and and_1 (and_1_out, d_ff_2_q, MIR[1]);
  D_Flip_Flop d_ff_1 (.clk(Clock), .D(ALU[1]), .Q(d_ff_1_q));  // open: Qn, preset, en, reset
  or or_1 (High_Bit, and_1_out, and_2_out);
  and and_2 (and_2_out, d_ff_1_q, MIR[0]);
  D_Flip_Flop d_ff_2 (.clk(Clock), .D(ALU[0]), .Q(d_ff_2_q));  // open: Qn, preset, en, reset
endmodule

module RAM (
  input  [31:0] MAR,
  input  [31:0] PC,
  input  Read,
  input  Fetch,
  input  \type ,
  input  Write,
  input  [31:0] MDRIN,
  input  clear,
  input  clear_2,
  output [31:0] MDROUT,
  output [7:0] MBR
);

  wire decoder_1_out0, decoder_1_out1, decoder_1_out2, decoder_1_out3, decoder_2_out0, decoder_2_out1,
       decoder_2_out2, decoder_2_out3, not_1_out, not_2_out, not_3_out;
  wire [1:0] bit_extender_1_out_2, clock_1_out;
  wire [7:0] multiplexer_1_out, ram_1_data, register_1_q, register_2_q, register_3_q, register_4_q,
       register_5_q, register_6_q, register_7_q, register_8_q;
  wire [21:0] bit_extender_1_out;
  wire [23:0] controlled_buffer_3_out;
  wire [31:0] controlled_buffer_1_out, controlled_buffer_2_out;

  assign controlled_buffer_1_out = not_1_out ? MAR : 32'bz;  // Controlled_Buffer controlled_buffer_1
  // Probe on register_1_q
  // Probe on clock_1_out
  not not_1 (not_1_out, Fetch);
  Bit_Extender #(.in_width(32), .out_width(24)) bit_extender_1 (
    .in(controlled_buffer_1_out), .out({bit_extender_1_out_2, bit_extender_1_out}));
  Clock clock_1 (.out(clock_1_out[0]));
  Clock #(.highDuration(2), .lowDuration(2)) clock_2 (.out(clock_1_out[1]));
  Multiplexer #(.select(2), .width(8)) multiplexer_1 (
    .in0(register_1_q), .in1(register_2_q), .in2(register_3_q), .in3(register_4_q), .out(multiplexer_1_out),
    .sel(clock_1_out));  // open: en
  // Probe on register_2_q
  // Probe on register_3_q
  // Probe on register_4_q
  Decoder #(.select(2)) decoder_1 (
    .out0(decoder_1_out0), .out1(decoder_1_out1), .out2(decoder_1_out2), .out3(decoder_1_out3),
    .sel(clock_1_out));  // open: en
  assign controlled_buffer_2_out = Fetch ? PC : 32'bz;  // Controlled_Buffer controlled_buffer_2
  Bit_Extender #(.in_width(32), .out_width(24)) bit_extender_2 (
    .in(controlled_buffer_2_out), .out({bit_extender_1_out_2, bit_extender_1_out}));
  assign controlled_buffer_3_out = not_2_out ? {bit_extender_1_out_2, bit_extender_1_out} : 24'bz;  // Controlled_Buffer controlled_buffer_3
  not not_2 (not_2_out, \type );
  assign controlled_buffer_3_out = \type  ? {bit_extender_1_out, clock_1_out} : 24'bz;  // Controlled_Buffer controlled_buffer_4
  // Probe on multiplexer_1_out
  Register #(.trigger("falling")) register_1 (
    .D(MDRIN[7:0]), .Q(register_1_q), .clk(decoder_1_out0), .clr(clear_2));  // open: en
  Register #(.trigger("falling")) register_2 (
    .D(MDRIN[15:8]), .Q(register_2_q), .clk(decoder_1_out1), .clr(clear_2));  // open: en
  Register #(.trigger("falling")) register_3 (
    .D(MDRIN[23:16]), .Q(register_3_q), .clk(decoder_1_out2), .clr(clear_2));  // open: en
  Register #(.trigger("falling")) register_4 (
    .D(MDRIN[31:24]), .Q(register_4_q), .clk(decoder_1_out3), .clr(clear_2));  // open: en
  RAM_part #(.addrWidth(24)) ram_1 (
    .addr(controlled_buffer_3_out), .data(ram_1_data), .clk(clock_1_out[0]), .ld(not_3_out));  // open: sel, clr
  not not_3 (not_3_out, Write);
  assign ram_1_data = Write ? multiplexer_1_out : 8'bz;  // Controlled_Buffer controlled_buffer_5
  Decoder #(.select(2)) decoder_2 (
    .out0(decoder_2_out0), .out1(decoder_2_out1), .out2(decoder_2_out2), .out3(decoder_2_out3),
    .sel(clock_1_out));  // open: en
  Register #(.trigger("falling")) register_5 (
    .D(ram_1_data), .Q(register_5_q), .clk(decoder_2_out0), .clr(clear));  // open: en
  // Probe on register_5_q
  Register #(.trigger("falling")) register_6 (
    .D(ram_1_data), .Q(register_6_q), .clk(decoder_2_out1), .clr(clear));  // open: en
  // Probe on register_6_q
  // Probe on register_7_q
  Register #(.trigger("falling")) register_7 (
    .D(ram_1_data), .Q(register_7_q), .clk(decoder_2_out2), .clr(clear));  // open: en
  // Probe on register_8_q
  Register #(.trigger("falling")) register_8 (
    .D(ram_1_data), .Q(register_8_q), .clk(decoder_2_out3), .clr(clear));  // open: en
  assign MDROUT = Read ? {register_8_q, register_7_q, register_6_q, register_5_q} : 32'bz;  // Controlled_Buffer controlled_buffer_6
  assign MBR = Fetch ? controlled_buffer_2_out[7:0] : 8'bz;  // Controlled_Buffer controlled_buffer_7
endmodule
